# Fritzing sketch Autohelm 800 ESP32 Retrofit v2 (saved by Fritzing 0.9.6b)
circuit board: 8.46667cm x 5.64444cm

parts:
  JP1 = Header 5x2 [package=avr_icsp]
  J1 = Power Jack [package=power_jack_smd]
  M1 = DC Motor
  U2 = Mini-360 DC-DC Buck converter [package=THT]
  DRV8871 = Adafruit DRV8871 [part_number="Adafruit #3190"]
  Part2 = ACS712 Low Current Sensor Board v12
  U3 = ESP32-38PinWide [part_number=ESP32-38PinWide]

nets:
  N1: JP1.3, U3.GPIO2
  N2: JP1.5, U3.GPIO0
  N3: JP1.6, U3.GPIO17
  N4: JP1.7, U3.GPIO4
  GND: JP1.8, U2.OUT-, DRV8871.GND, Part2.GND, Part2.IP+, U3.GND
  N5: JP1.9, U3.GPIO16
  N6: JP1.10, U3.GPIO5
  N7: J1.GND, U2.IN-, Part2.IP-
  N8: J1.GNDBREAK, U2.IN+, DRV8871.VMOTOR
  N9: M1.pin_1, DRV8871.OUT2
  N10: M1.pin_2, DRV8871.OUT1
  5V: U2.OUT+, Part2.5V, U3.VIN
  N11: DRV8871.IN1, U3.GPIO32
  N12: DRV8871.IN2, U3.GPIO33
  N13: Part2.VO, U3.GPIO13

notes:
  Keypad : AutoHelm 800
  HBridge : DRV8871
  Current Sensor : ACS712
  Power Down : Mini-360

custom parts:
  Mini-360 DC-DC Buck converter: Mini-360 DC-DC Buck converter. Tiny buck step down voltage converter, input voltage 4.75 to 23V output 1 to 17V adjustable. Available from ebay and the like.
  Adafruit DRV8871: Crank up your robotics with powerful Adafruit DRV8871 motor driver breakout board. This motor driver has a lot of great specs that make it useful for a wide variety of mechatronics. In particular, the simple resistor-set current limiting and auto-magic PWM support make it super easy to use. Check out the specs for the DRV8871: 6.5V to 45V motor power voltage Up to 5.5V logic level on IN pins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
  ESP32-38PinWide: Generic 38-Pin ESP32 with wide format (only access to one side of pins on a breadboard) based on Stephen Lilley's HiLetgo ESP-WROOM-32 ESP32 ESP-32S Development Board.
